# Fritzing sketch Circuito con Bottone (saved by Fritzing 0.7.12b)
breadboards: 1

parts:
  Arduino1 = Arduino
  R1 = Resistor [tolerance=±5% resistance=220 package=THT]
  S1 = Pushbutton [package="[THT]"]
  LED1 = LED - 5mm [color="Red (633nm)" package="5 mm [THT]"]

nets:
  N1: Arduino1.+5V, R1.Pin_0
  N2: Arduino1.GND, LED1.cathode
  N3: R1.Pin_1, S1.Pin_1, S1.Pin_2
  N4: S1.Pin_3, LED1.anode
