# Fritzing sketch Circuito in Parallelo (saved by Fritzing 0.8.0b)
breadboards: 1

parts:
  Componente1 = Arduino Uno (Rev3)
  R1 = Resistor [tolerance=±5% resistance=220 package=THT]
  S1 = Pushbutton [package="[THT]"]
  S2 = Pushbutton [package="[THT]"]
  LED1 = LED - 5mm [color="Red (633nm)" package="5 mm [THT]"]

nets:
  N1: Componente1.GND, LED1.cathode
  N2: Componente1.5V, R1.Pin_0
  N3: R1.Pin_1, S1.Pin_3, S1.Pin_4, S2.Pin_3, S2.Pin_4, LED1.anode
