# Fritzing sketch Un Semplice Circuito Elettrico (saved by Fritzing 0.7.12b)
breadboards: 1

parts:
  Arduino1 = Arduino
  LED1 = LED - 5mm [color="Red (633nm)" package="5 mm [THT]"]
  R1 = Resistor [tolerance=±5% resistance=220 package=THT]

nets:
  N1: Arduino1.GND, R1.Pin_0
  N2: Arduino1.+5V, LED1.anode
  N3: LED1.cathode, R1.Pin_1
